// Logisim project coconut16.circ as structural Verilog: 9 circuits, main circuit main
module main (
  input  [19:0] in_1
);

  wire and_2_out, and_3_out, and_4_out, and_6_out, bus_mem, bus_rd_wr_prime, bus_word, button_1_out,
       button_2_out, button_3_out, clk, comparator_1_eq, comparator_1_gt, comparator_1_lt, comparator_2_eq,
       comparator_2_gt, comparator_2_lt, data_ins_prime, decoder_1_out0, decoder_1_out1, decoder_1_out2,
       decoder_1_out3, decoder_2_out1, decoder_2_out2, decoder_2_out3, dma_device_rd_wr_prime, dma_iack,
       dma_irq, dma_mem, dma_rd_wr_prime, exc, fetch, hold, iack, int_arbiter_1_ack_out, int_arbiter_2_ack,
       int_arbiter_2_ack_out, int_arbiter_2_irq_out, int_arbiter_3_irq_out, int_en, io_ack, io_header,
       io_sel, irq, mem, mmu_1_exception, mode, not_2_out, or_1_out, or_3_out, processor_mem, processor_wait,
       ram_sel, rd_wr_prime, rom_sel, single_step_1_run, single_step_1_stop, timer_1_irq,
       uart_controller_1_irq, vec, word;
  wire [1:0] mmu_1_exception_number, status;
  wire [2:0] exc_vec;
  wire [5:0] int_vec;
  wire [7:0] context_number, ctx_number;
  wire [11:0] io_bus_address;
  wire [12:0] ps;
  wire [15:0] cdm16e_1_p29, cdm16e_1_p30, data, dma_device_data, fp, pc, r0, r1, r2, r3, r4, r5, r6, sp,
       status_code, timer_1_mon, virtual_address;
  wire [19:0] address_bus, dma_ram_addr, physical_address;
  wire [23:0] bit_extender_1_out;
  wire [31:0] dma_1_device_address;

  // Probe on fp
  // Probe on r6
  // Probe on r5
  // Probe on r4
  // Probe on r3
  // Probe on r2
  // Probe on r1
  // Probe on r0
  Button button_1 (.out(button_1_out));
  Button button_2 (.out(button_2_out));
  LED led_1 (.in(single_step_1_run));
  LED led_2 (.in(single_step_1_stop));
  single_step single_step_1 (
    .btn_stop(button_1_out), .btn_run(button_2_out), .btn_step(button_3_out), .clk(clk), .fetch(fetch),
    .hold(hold), .stop(single_step_1_stop), .run(single_step_1_run));
  Clock clock_1 (.out(clk));
  // NOT_Gate not_1 is placed but not wired
  LED led_3 (.in(int_en));
  // cdm16e cdm16e_1: pin names not known; wires that end beside it: irq, int_vec, iack, exc, {3'b001, exc_vec}, hold, r0, r1, clk, r2, r3, r4, status, r5, r6, fp, fetch, pc, sp, {int_en, mode, io_header, ps[12], ctx_number, ps[3:0]}, io_header, data_ins_prime, processor_mem, rd_wr_prime, word, vec, virtual_address, context_number, cdm16e_1_p29, cdm16e_1_p30
  and and_1 (processor_wait, status[0], ~status[1]);  // AND_Gate
  Button button_3 (.out(button_3_out));
  DMA dma_1 (
    .mem(mem), .io(io_sel), .iack(dma_iack), .device_data_in(dma_device_data), .bus_data_in(data),
    .Address(io_bus_address), .RAM_register_addr(12'hf70), .Sector_no_reg_addr(12'hf72),
    .Control_reg_addr(12'hf76), .Clock(clk), .RAM_rd_wr_prime(dma_rd_wr_prime),
    .Device_rd_wr_prime(dma_device_rd_wr_prime), .Device_address(dma_1_device_address),
    .device_data_out(dma_device_data), .bus_data_out(data), .RAM_address(dma_ram_addr), .IRQ(dma_irq),
    .mem_2(dma_mem), .rd_wr_prime(bus_rd_wr_prime), .io_ack(io_ack));
  LED led_4 (.in(mode));
  LED led_5 (.in(io_header));
  // Probe on ctx_number
  // Probe on pc
  // Probe on sp
  // Probe on {int_en, mode, io_header, ps[12], ctx_number, ps[3:0]}
  assign cdm16e_1_p30 = and_3_out ? data : 16'bz;  // Controlled_Buffer controlled_buffer_1
  Bit_Extender #(.in_width(32), .out_width(24)) bit_extender_1 (.in(dma_1_device_address), .out(bit_extender_1_out));
  assign data = and_2_out ? cdm16e_1_p29 : 16'bz;  // Controlled_Buffer controlled_buffer_2
  not not_2 (not_2_out, rd_wr_prime);
  and and_2 (and_2_out, not_2_out, mem);
  and and_3 (and_3_out, mem, rd_wr_prime);
  LED led_6 (.in(decoder_1_out0));
  Decoder #(.select(2), .disabled(0), .enable("false")) decoder_1 (
    .out0(decoder_1_out0), .out1(decoder_1_out1), .out2(decoder_1_out2), .out3(decoder_1_out3), .sel(status));
  LED led_7 (.in(decoder_1_out1));
  LED led_8 (.in(decoder_1_out2));
  LED led_9 (.in(decoder_1_out3));
  Hex_Digit_Display hex_digit_display_1 (.value(status_code[15:12]));  // open: dp
  // RAM ram_1: pin names not known; wires that end beside it: bit_extender_1_out, 1'b1, dma_mem, clk, dma_device_rd_wr_prime, dma_device_data
  Pull_Resistor pull_resistor_1 (.node(bus_rd_wr_prime));
  Pull_Resistor pull_resistor_2 (.node(bus_word));
  Pull_Resistor pull_resistor_3 (.node(address_bus));
  Hex_Digit_Display hex_digit_display_2 (.value(status_code[7:4]));  // open: dp
  Hex_Digit_Display hex_digit_display_3 (.value(status_code[11:8]));  // open: dp
  MMU mmu_1 (
    .Virtual_address(virtual_address), .Context_number(context_number), .Data(data_ins_prime),
    .Clock__generator(clk), .Physical_address(physical_address), .Exception(mmu_1_exception), .Vector(vec),
    .IO_enable(io_header), .Data_In(data), .Data_out(data), .Context_register_address(12'hf7e),
    .Table_address(12'hf80), .rd_wr_prime(rd_wr_prime), .Exception_number(mmu_1_exception_number),
    .Exception_address_register(12'hf7c), .io_ack(io_ack), .mem(processor_mem));
  Pull_Resistor pull_resistor_4 (.node(io_ack));
  assign bus_rd_wr_prime = dma_mem ? dma_rd_wr_prime : 1'bz;  // Controlled_Buffer controlled_buffer_3
  assign bus_word = dma_mem ? 1'b1 : 1'bz;  // Controlled_Buffer controlled_buffer_4
  assign address_bus = dma_mem ? dma_ram_addr : 20'bz;  // Controlled_Buffer controlled_buffer_5
  Hex_Digit_Display hex_digit_display_4 (.value(status_code[3:0]));  // open: dp
  // Probe on physical_address
  Decoder #(.select(2), .disabled(0)) decoder_2 (
    .out1(decoder_2_out1), .out2(decoder_2_out2), .out3(decoder_2_out3), .sel(mmu_1_exception_number),
    .en(mmu_1_exception));  // open: out0
  and and_4 (and_4_out, io_sel, ~io_ack);  // AND_Gate
  assign bus_rd_wr_prime = mem ? rd_wr_prime : 1'bz;  // Controlled_Buffer controlled_buffer_6
  assign bus_word = mem ? word : 1'bz;  // Controlled_Buffer controlled_buffer_7
  assign address_bus = mem ? physical_address : 20'bz;  // Controlled_Buffer controlled_buffer_8
  Bit_Extender #(.in_width(20), .out_width(12)) bit_extender_2 (.in(address_bus), .out(io_bus_address));
  and and_5 (mem, processor_mem, ~processor_wait, ~mmu_1_exception);  // AND_Gate
  Priority_Encoder #(.disabled(0)) priority_encoder_1 (
    .in0(decoder_2_out1), .in1(decoder_2_out2), .in2(decoder_2_out3), .in3(and_4_out), .out(exc_vec),
    .en_in(processor_mem), .gs(exc));  // open: in4, in5, in6, in7, en_out
  int_arbiter int_arbiter_1 (
    .vec_in(6'b010000), .irq_out(irq), .ack_in(iack), .vec_out(int_vec), .ack(dma_iack),
    .irq_in(int_arbiter_2_irq_out), .ack_out(int_arbiter_1_ack_out), .req(dma_irq));  // open: nop, req_2, ack_2
  int_arbiter int_arbiter_2 (
    .vec_in(6'b010001), .irq_out(int_arbiter_2_irq_out), .ack_in(int_arbiter_1_ack_out), .vec_out(int_vec),
    .ack(int_arbiter_2_ack), .irq_in(int_arbiter_3_irq_out), .ack_out(int_arbiter_2_ack_out),
    .req(timer_1_irq));  // open: nop, req_2, ack_2
  // Probe on timer_1_mon
  timer timer_1 (
    .data_out(data), .data_in(data), .address(12'hf58), .io_address(io_bus_address), .io_sel(io_sel),
    .rd_wr_prime(bus_rd_wr_prime), .clk(clk), .iack(int_arbiter_2_ack), .irq(timer_1_irq), .mon(timer_1_mon),
    .io_ack(io_ack));
  register register_1 (
    .data_out(data), .data_in(data), .address(12'hf40), .io_address(io_bus_address), .io_sel(io_sel),
    .rd_wr_prime(bus_rd_wr_prime), .clk(clk), .io_ack(io_ack), .mon(status_code));
  Comparator #(.width(20), .mode("unsigned")) comparator_1 (
    .a(address_bus), .b(20'hff000), .gt(comparator_1_gt), .eq(comparator_1_eq), .lt(comparator_1_lt));
  or or_1 (or_1_out, comparator_2_gt, comparator_2_eq);
  Comparator #(.width(20), .mode("unsigned")) comparator_2 (
    .a(address_bus), .b(20'hfe000), .gt(comparator_2_gt), .eq(comparator_2_eq), .lt(comparator_2_lt));
  // RAM ram_2: pin names not known; wires that end beside it: address_bus, bus_word, ram_sel, clk, bus_rd_wr_prime, data
  // UART uart_1: pin names not known; wires that end beside it: clk, io_ack, io_bus_address, io_sel, bus_rd_wr_prime, bus_word, data
  or or_2 (bus_mem, mem, dma_mem);
  or or_3 (or_3_out, comparator_1_gt, comparator_1_eq);
  and and_6 (and_6_out, comparator_1_lt, or_1_out);
  int_arbiter int_arbiter_3 (
    .vec_in(6'b010100), .irq_out(int_arbiter_3_irq_out), .ack_in(int_arbiter_2_ack_out), .vec_out(int_vec),
    .req(uart_controller_1_irq));  // open: ack, irq_in, ack_out, nop, req_2, ack_2
  uart_controller uart_controller_1 (
    .data_out(data), .data_in(data), .io_sel(io_sel), .rd_wr_prime(bus_rd_wr_prime), .clk(clk),
    .io_ack(io_ack), .base_address(12'hf50), .io_address(io_bus_address), .word(bus_word),
    .irq(uart_controller_1_irq));  // open: uart_dt, uart_rx, uart_con, uart_clk, uart_rd_wr_prime, uart_en, uart_tx
  and and_7 (io_sel, or_3_out, bus_mem);
  and and_8 (rom_sel, and_6_out, bus_mem);
  and and_9 (ram_sel, comparator_2_lt, bus_mem);
  // ROM rom_1: pin names not known; wires that end beside it: io_bus_address, rom_sel, bus_word, data

  // Other names for the same wires on the sheet: ps (some bits) = {int_en, mode, io_header, ctx_number};
  //   rom_bus_address[11:0] = io_bus_address

  // Notes on the sheet:
  //   Run
  //   Wait
  //   Halt
  //   Fault
endmodule

module debug (
  input  [19:0] in_1
);

  wire and_2_out, and_3_out, and_5_out, bus_mem, bus_rd_wr_prime, bus_word, button_1_out, button_2_out,
       button_3_out, clk, comparator_1_eq, comparator_1_gt, comparator_1_lt, comparator_2_eq,
       comparator_2_gt, comparator_2_lt, data_ins_prime, decoder_1_out0, decoder_1_out1, decoder_1_out2,
       decoder_1_out3, dma_iack, dma_irq, fetch, hold, iack, int_arbiter_1_ack_out, int_arbiter_2_ack,
       int_arbiter_2_ack_out, int_arbiter_2_irq_out, int_arbiter_3_irq_out, int_en, io_ack, io_header,
       io_sel, irq, mem, mode, not_2_out, or_1_out, or_2_out, or_4_out, processor_mem, processor_wait,
       ram_sel, rd_wr_prime, rom_sel, single_step_1_run, single_step_1_stop, timer_1_irq,
       uart_controller_1_irq, word;
  wire [1:0] status;
  wire [5:0] exc_vec, int_vec;
  wire [7:0] context_number, ctx_number;
  wire [11:0] io_bus_address;
  wire [12:0] ps;
  wire [15:0] address_bus, cdm16_1_p27, cdm16_1_p28, data, fp, pc, physical_address, r0, r1, r2, r3, r4, r5,
       r6, sp, status_code, timer_1_mon;

  // Probe on fp
  // Probe on r6
  // Probe on r5
  // Probe on r4
  // Probe on r3
  // Probe on r2
  // Probe on r1
  // Probe on r0
  Button button_1 (.out(button_1_out));
  Button button_2 (.out(button_2_out));
  LED led_1 (.in(single_step_1_run));
  single_step single_step_1 (
    .btn_stop(button_2_out), .btn_run(button_1_out), .btn_step(button_3_out), .clk(clk), .fetch(fetch),
    .hold(hold), .stop(single_step_1_stop), .run(single_step_1_run));
  LED led_2 (.in(single_step_1_stop));
  Clock clock_1 (.out(clk));
  // NOT_Gate not_1 is placed but not wired
  LED led_3 (.in(int_en));
  // cdm16 cdm16_1: pin names not known; wires that end beside it: irq, int_vec, iack, exc_vec, hold, r0, r1, clk, r2, r3, r4, status, r5, r6, fp, fetch, pc, sp, {int_en, mode, io_header, ps[12], ctx_number, ps[3:0]}, io_header, data_ins_prime, processor_mem, rd_wr_prime, word, physical_address, context_number, cdm16_1_p27, cdm16_1_p28
  and and_1 (processor_wait, status[0], ~status[1]);  // AND_Gate
  Button button_3 (.out(button_3_out));
  LED led_4 (.in(mode));
  LED led_5 (.in(io_header));
  // Probe on ctx_number
  // Probe on pc
  // Probe on sp
  // Probe on {int_en, mode, io_header, ps[12], ctx_number, ps[3:0]}
  assign cdm16_1_p28 = and_3_out ? data : 16'bz;  // Controlled_Buffer controlled_buffer_1
  assign data = and_2_out ? cdm16_1_p27 : 16'bz;  // Controlled_Buffer controlled_buffer_2
  not not_2 (not_2_out, rd_wr_prime);
  and and_2 (and_2_out, not_2_out, mem);
  and and_3 (and_3_out, mem, rd_wr_prime);
  LED led_6 (.in(decoder_1_out0));
  Decoder #(.select(2), .disabled(0), .enable("false")) decoder_1 (
    .out0(decoder_1_out0), .out1(decoder_1_out1), .out2(decoder_1_out2), .out3(decoder_1_out3), .sel(status));
  LED led_7 (.in(decoder_1_out1));
  LED led_8 (.in(decoder_1_out2));
  LED led_9 (.in(decoder_1_out3));
  Hex_Digit_Display hex_digit_display_1 (.value(status_code[15:12]));  // open: dp
  // Probe on physical_address
  // Probe on physical_address
  // Debugger debugger_1: pin names not known; wires that end beside it: in_1
  Pull_Resistor pull_resistor_1 (.node(bus_rd_wr_prime));
  Pull_Resistor pull_resistor_2 (.node(bus_word));
  Pull_Resistor pull_resistor_3 (.node(address_bus));
  Hex_Digit_Display hex_digit_display_2 (.value(status_code[11:8]));  // open: dp
  Hex_Digit_Display hex_digit_display_3 (.value(status_code[7:4]));  // open: dp
  Hex_Digit_Display hex_digit_display_4 (.value(status_code[3:0]));  // open: dp
  assign bus_rd_wr_prime = mem ? rd_wr_prime : 1'bz;  // Controlled_Buffer controlled_buffer_3
  assign bus_word = mem ? word : 1'bz;  // Controlled_Buffer controlled_buffer_4
  assign address_bus = mem ? physical_address : 16'bz;  // Controlled_Buffer controlled_buffer_5
  Bit_Extender #(.in_width(16), .out_width(12)) bit_extender_1 (.in(address_bus), .out(io_bus_address));
  int_arbiter int_arbiter_1 (
    .vec_in(6'b010000), .irq_out(irq), .ack_in(iack), .vec_out(int_vec), .ack(dma_iack),
    .irq_in(int_arbiter_2_irq_out), .ack_out(int_arbiter_1_ack_out), .req(dma_irq));  // open: nop, req_2, ack_2
  or or_1 (or_1_out, ram_sel, rom_sel);
  int_arbiter int_arbiter_2 (
    .vec_in(6'b010001), .irq_out(int_arbiter_2_irq_out), .ack_in(int_arbiter_1_ack_out), .vec_out(int_vec),
    .ack(int_arbiter_2_ack), .irq_in(int_arbiter_3_irq_out), .ack_out(int_arbiter_2_ack_out),
    .req(timer_1_irq));  // open: nop, req_2, ack_2
  // Probe on timer_1_mon
  timer timer_1 (
    .data_out(data), .data_in(data), .address(12'hf58), .io_address(io_bus_address), .io_sel(io_sel),
    .rd_wr_prime(bus_rd_wr_prime), .clk(clk), .iack(int_arbiter_2_ack), .irq(timer_1_irq), .mon(timer_1_mon),
    .io_ack(io_ack));
  register register_1 (
    .data_out(data), .data_in(data), .address(12'hf40), .io_address(io_bus_address), .io_sel(io_sel),
    .rd_wr_prime(bus_rd_wr_prime), .clk(clk), .io_ack(io_ack), .mon(status_code));
  Comparator #(.width(16), .mode("unsigned")) comparator_1 (
    .a(address_bus), .b(16'hff00), .gt(comparator_1_gt), .eq(comparator_1_eq), .lt(comparator_1_lt));
  or or_2 (or_2_out, comparator_2_gt, comparator_2_eq);
  Comparator #(.width(16), .mode("unsigned")) comparator_2 (
    .a(address_bus), .b(16'hfe00), .gt(comparator_2_gt), .eq(comparator_2_eq), .lt(comparator_2_lt));
  and and_4 (mem, processor_mem, ~processor_wait);  // AND_Gate
  // RAM ram_1: pin names not known; wires that end beside it: address_bus, bus_word, or_1_out, clk, bus_rd_wr_prime, data
  // UART uart_1: pin names not known; wires that end beside it: clk, io_ack, io_bus_address, io_sel, bus_rd_wr_prime, bus_word, data
  buf or_3 (bus_mem, mem);  // OR_Gate
  or or_4 (or_4_out, comparator_1_gt, comparator_1_eq);
  and and_5 (and_5_out, comparator_1_lt, or_2_out);
  int_arbiter int_arbiter_3 (
    .vec_in(6'b010100), .irq_out(int_arbiter_3_irq_out), .ack_in(int_arbiter_2_ack_out), .vec_out(int_vec),
    .req(uart_controller_1_irq));  // open: ack, irq_in, ack_out, nop, req_2, ack_2
  uart_controller uart_controller_1 (
    .data_out(data), .data_in(data), .io_sel(io_sel), .rd_wr_prime(bus_rd_wr_prime), .clk(clk),
    .io_ack(io_ack), .base_address(12'hf50), .io_address(io_bus_address), .word(bus_word),
    .irq(uart_controller_1_irq));  // open: uart_dt, uart_rx, uart_con, uart_clk, uart_rd_wr_prime, uart_en, uart_tx
  and and_6 (io_sel, or_4_out, bus_mem);
  and and_7 (rom_sel, and_5_out, bus_mem);
  and and_8 (ram_sel, comparator_2_lt, bus_mem);

  // Other names for the same wires on the sheet: ps (some bits) = {int_en, mode, io_header, ctx_number};
  //   virtual_address[15:0] = physical_address

  // Notes on the sheet:
  //   Run
  //   Wait
  //   Halt
  //   Fault
endmodule

module MMU (
  input  IO_enable,
  input  Vector,
  input  rd_wr_prime,
  input  mem,
  input  [15:0] Data_In,
  input  [15:0] Virtual_address,
  input  [7:0] Context_number,
  input  Data,
  input  Clock__generator,
  input  [11:0] Context_register_address,
  input  [11:0] Exception_address_register,
  input  [11:0] Table_address,
  output [19:0] Physical_address,
  output [1:0] Exception_number,
  output Exception,
  output [15:0] Data_out,
  output io_ack
);

  wire and_5_out, and_6_out, and_7_out, and_8_out, comparator_1_eq, comparator_2_eq, comparator_3_gt,
       comparator_4_gt, comparator_6_lt, comparator_7_lt, comparator_8_gt, Context_register_select,
       controlled_buffer_1_out, Device_area, Exception_register_select, Flags_table_select, Inverse_bit,
       io_ack_t, multiplexer_2_out, not_1_out, not_2_out, not_3_out, not_4_out, not_5_out, not_6_out,
       not_7_out, not_8_out, or_1_out, Paragraph_offset_select, Presence_bit, Table_select, Translation,
       Use_constants;
  wire [1:0] priority_encoder_1_out, priority_encoder_2_out;
  wire [1:1] Segment_flags;
  wire [7:0] Context_register, multiplexer_1_out;
  wire [11:0] adder_1_out, subtractor_1_out;
  wire [12:0] multiplexer_5_out, multiplexer_6_out, Segment_info;
  wire [15:0] bit_extender_2_out, Exception_address, Paragraph_offset;
  wire [19:0] adder_2_out, bit_extender_1_out, Device_area_Address, subtractor_2_out, Vector_Address;

  Adder #(.width(12)) adder_1 (.a(Table_address), .b(12'h7f), .out(adder_1_out));  // open: cin, cout
  and and_1 (Context_register_select, Device_area, comparator_1_eq);
  Comparator #(.width(12), .mode("unsigned")) comparator_1 (
    .a(Virtual_address[11:0]), .b(Context_register_address), .eq(comparator_1_eq));  // open: gt, lt
  and and_2 (Exception_register_select, Device_area, comparator_2_eq);
  Comparator #(.width(12), .mode("unsigned")) comparator_2 (
    .a(Virtual_address[11:0]), .b(Exception_address_register), .eq(comparator_2_eq));  // open: gt, lt
  not not_1 (not_1_out, comparator_3_gt);
  Comparator #(.width(12), .mode("unsigned")) comparator_3 (
    .a(Table_address), .b(Virtual_address[11:0]), .gt(comparator_3_gt));  // open: eq, lt
  not not_2 (not_2_out, comparator_4_gt);
  Comparator #(.width(12), .mode("unsigned")) comparator_4 (
    .a(Virtual_address[11:0]), .b(adder_1_out), .gt(comparator_4_gt));  // open: eq, lt
  Register register_1 (
    .D(Data_In[7:0]), .en(Context_register_select), .Q(Context_register), .clk(Clock__generator));  // open: clr
  and and_3 (Table_select, not_1_out, not_2_out, Device_area);
  // Probe on Paragraph_offset
  Demultiplexer #(.disabled(0)) demultiplexer_1 (
    .out0(Flags_table_select), .out1(Paragraph_offset_select), .in(Table_select), .sel(Virtual_address[6]),
    .en(not_3_out));
  not not_3 (not_3_out, rd_wr_prime);
  // Probe on Segment_info[7:0]
  Multiplexer #(.width(8), .enable("false")) multiplexer_1 (
    .in0(Context_number), .in1(Context_register), .out(multiplexer_1_out), .sel(Device_area));
  Comparator comparator_5 (.a(multiplexer_1_out), .b({8{1'b0}}), .eq(Use_constants));  // open: gt, lt
  assign bit_extender_1_out = {{8{1'b0}}, Virtual_address[11:0]};  // Bit_Extender bit_extender_1
  not not_4 (not_4_out, Use_constants);
  Comparator #(.width(12), .mode("unsigned")) comparator_6 (
    .a(Virtual_address[11:0]), .b({Segment_info[7:0], 4'b0000}), .lt(comparator_6_lt));  // open: gt, eq
  ROM #(.addrWidth(5), .dataWidth(32)) rom_1 (
    .addr({Data, Virtual_address[15:12]}),
    .data({Paragraph_offset, Presence_bit, Segment_flags[1], Inverse_bit, Segment_info}), .sel(Use_constants));
  Adder #(.width(20)) adder_2 (
    .a({Paragraph_offset, 4'b0000}), .b(bit_extender_1_out), .out(adder_2_out));  // open: cin, cout
  assign controlled_buffer_1_out = not_4_out ? Vector : 1'bz;  // Controlled_Buffer controlled_buffer_1
  Pull_Resistor pull_resistor_1 (.node(controlled_buffer_1_out));
  not not_5 (not_5_out, comparator_6_lt);
  Subtractor #(.width(12)) subtractor_1 (
    .a({12{1'b1}}), .b({Segment_info[7:0], 4'b0000}), .out(subtractor_1_out));  // open: bin, bout
  Comparator #(.width(12), .mode("unsigned")) comparator_7 (
    .a(subtractor_1_out), .b(Virtual_address[11:0]), .lt(comparator_7_lt));  // open: gt, eq
  Comparator #(.mode("unsigned")) comparator_8 (
    .a(Segment_info[7:0]), .b({8{1'b0}}), .gt(comparator_8_gt));  // open: eq, lt
  LED led_1 (.in(Inverse_bit));
  LED led_2 (.in(Segment_flags[1]));
  LED led_3 (.in(Presence_bit));
  and and_4 (Device_area, Virtual_address[12], Virtual_address[13], Virtual_address[14], Virtual_address[15], Data, IO_enable);
  Subtractor #(.width(20)) subtractor_2 (.a(adder_2_out), .b(20'h1000), .out(subtractor_2_out));  // open: bin, bout
  Multiplexer #(.disabled(0)) multiplexer_2 (
    .in0(not_5_out), .in1(not_6_out), .out(multiplexer_2_out), .sel(Inverse_bit), .en(comparator_8_gt));
  not not_6 (not_6_out, comparator_7_lt);
  assign bit_extender_2_out = {{8{1'b0}}, Context_register};  // Bit_Extender bit_extender_2
  Priority_Encoder #(.select(2)) priority_encoder_1 (
    .in0(1'b1), .in1(Virtual_address[6]), .in2(Context_register_select), .in3(Exception_register_select),
    .out(priority_encoder_1_out));  // open: gs, en_out, en_in
  Multiplexer #(.select(2), .width(20), .enable("false")) multiplexer_3 (
    .in0(adder_2_out), .in1(subtractor_2_out), .in2(Vector_Address), .in3(Device_area_Address),
    .out(Physical_address), .sel(priority_encoder_2_out));
  Priority_Encoder #(.select(2)) priority_encoder_2 (
    .in0(1'b1), .in1(Inverse_bit), .in2(controlled_buffer_1_out), .in3(Device_area),
    .out(priority_encoder_2_out));  // open: gs, en_out, en_in
  and and_5 (and_5_out, rd_wr_prime, or_1_out);
  or or_1 (or_1_out, Context_register_select, Exception_register_select, Table_select);
  and and_6 (and_6_out, Segment_flags[1], Translation, ~rd_wr_prime);  // AND_Gate
  and and_7 (and_7_out, Translation, mem);
  and and_8 (and_8_out, Translation, ~Presence_bit);  // AND_Gate
  Multiplexer #(.select(2), .width(16)) multiplexer_4 (
    .in0({Presence_bit, Segment_flags[1], Inverse_bit, Segment_info}), .in1(Paragraph_offset),
    .in2(bit_extender_2_out), .in3(Exception_address), .out(Data_out), .sel(priority_encoder_1_out),
    .en(and_5_out));
  Register #(.width(16), .trigger("falling")) register_2 (
    .D(Virtual_address), .en(Exception), .Q(Exception_address), .clk(Clock__generator));  // open: clr
  Priority_Encoder #(.select(2)) priority_encoder_3 (
    .in1(and_6_out), .in2(multiplexer_2_out), .in3(and_8_out), .out(Exception_number), .gs(Exception),
    .en_in(and_7_out));  // open: in0, en_out
  Multiplexer #(.width(13), .enable("false")) multiplexer_5 (
    .in0({Context_number, Data, Virtual_address[15:12]}), .in1({Context_register, Virtual_address[5:1]}),
    .out(multiplexer_5_out), .sel(Device_area));
  Multiplexer #(.width(13), .enable("false")) multiplexer_6 (
    .in0({Context_number, Data, Virtual_address[15:12]}), .in1({Context_register, Virtual_address[5:1]}),
    .out(multiplexer_6_out), .sel(Device_area));
  not not_7 (not_7_out, Use_constants);
  not not_8 (not_8_out, Use_constants);
  assign Vector_Address = {{4{1'b0}}, Virtual_address};  // Bit_Extender bit_extender_3
  assign Device_area_Address = {{4{1'b1}}, Virtual_address};  // Bit_Extender bit_extender_4
  Pull_Resistor pull_resistor_2 (.node({Presence_bit, Segment_flags[1], Inverse_bit, Segment_info}));
  RAM #(.addrWidth(13), .dataWidth(16), .bus("separate")) ram_1 (
    .addr(multiplexer_5_out), .din(Data_In),
    .data({Presence_bit, Segment_flags[1], Inverse_bit, Segment_info}), .str(Flags_table_select),
    .sel(not_8_out), .clk(Clock__generator), .ld(1'b1));  // open: clr
  RAM #(.addrWidth(13), .dataWidth(16), .bus("separate")) ram_2 (
    .addr(multiplexer_6_out), .din(Data_In), .data(Paragraph_offset), .str(Paragraph_offset_select),
    .sel(not_7_out), .clk(Clock__generator), .ld(1'b1));  // open: clr
  nor nor_1 (Translation, Device_area, Vector);
  or or_2 (io_ack_t, Exception_register_select, Context_register_select, Table_select);
  assign io_ack = io_ack_t ? 1'b1 : 1'bz;  // Controlled_Buffer controlled_buffer_2

  // Other names for the same wires on the sheet: Segment_length[7:0] = Segment_info[7:0];
  //   Segment_flags (some bits) = {Presence_bit, Inverse_bit};
  //   Segment_info[15:13] = {Presence_bit, Segment_flags[1], Inverse_bit}; Write_protect_bit = Segment_flags[1];
  //   Clock = Clock__generator; Descriptor_number[12:0] = {Context_number, Data, Virtual_address[15:12]};
  //   Inner_Des_Num[4:0] = {Data, Virtual_address[15:12]}; Segment_number[3:0] = Virtual_address[15:12];
  //   Device_mode_desriptor_number[12:0] = {Context_register, Virtual_address[5:1]};
  //   Inner_offset[11:0] = Virtual_address[11:0]

  // Notes on the sheet:
  //   Inputs
  //   Translation Inputs
  //   Number that processor wants to write
  //   Updates translation table when toggled
  //   from 0 to 1 in read/write mode
  //   or write protect bit and write wr'
  //   Inverse bit changes check for length
  //   Exceptions, if presence_bit == 0 and any access in translation mode
  //   Context
  //   Translation
  //   mode
  //   Outputs
  //   If zero context: map to ROM
  //   Paragraph length = 16
  //   contents of rom_1 (hex, n*v repeats v):
  //   fe008000 15*0 fd008000 13*0 8010
  //   Physical address getter
  //   Segment length and flags getter
  //   Paragraph offset getter
  //   If vector
  //   If device area
endmodule

module DMA (
  input  mem,
  input  io,
  input  iack,
  input  rd_wr_prime,
  input  [15:0] device_data_in,
  input  [15:0] bus_data_in,
  input  [11:0] Address,
  input  [11:0] RAM_register_addr,
  input  [11:0] Sector_no_reg_addr,
  input  [11:0] Control_reg_addr,
  input  Clock,
  output mem_2,
  output RAM_rd_wr_prime,
  output Device_rd_wr_prime,
  output [31:0] Device_address,
  output io_ack,
  output [15:0] device_data_out,
  output [15:0] bus_data_out,
  output [19:0] RAM_address,
  output IRQ
);

  wire _1_sector, _2_sector, and_1_out, and_2_out, and_3_out, and_8_out, and_9_out, and_10_out, Clock_t,
       comparator_1_eq, comparator_2_eq, comparator_3_eq, comparator_4_eq, Control_register_t, End, io_ack_t,
       not_1_out, not_2_out, not_3_out, not_4_out, not_5_out, not_6_out, not_7_out, not_9_out, or_1_out,
       or_3_out, or_4_out, or_5_out, priority_encoder_1_gs, RAM_address_t;
  wire [1:0] priority_encoder_1_out;
  wire [8:1] Counter;
  wire [11:0] adder_1_out;
  wire [15:0] Control_register, multiplexer_1_out, multiplexer_2_out, RAM_paragraph;
  wire [19:0] bit_extender_1_out, bit_extender_3_out, shifter_2_out;
  wire [31:0] bit_extender_2_out, Sector_no, shifter_1_out;

  not not_1 (not_1_out, mem);
  assign Clock_t = not_1_out ? Clock : 1'bz;  // Controlled_Buffer controlled_buffer_1
  Pull_Resistor pull_resistor_1 (.node(Clock_t));
  not not_2 (not_2_out, rd_wr_prime);
  and and_1 (and_1_out, not_2_out, RAM_address_t);
  not not_3 (not_3_out, rd_wr_prime);
  and and_2 (and_2_out, not_3_out, _1_sector);
  not not_4 (not_4_out, rd_wr_prime);
  and and_3 (and_3_out, not_4_out, _2_sector);
  Comparator #(.width(12)) comparator_1 (.a(Address), .b(RAM_register_addr), .eq(comparator_1_eq));  // open: gt, lt
  Adder #(.width(12)) adder_1 (.a(12'h1), .b(Sector_no_reg_addr), .out(adder_1_out));  // open: cin, cout
  Comparator #(.width(12)) comparator_2 (.a(Sector_no_reg_addr), .b(Address), .eq(comparator_2_eq));  // open: gt, lt
  Comparator #(.width(12)) comparator_3 (.a(Address), .b(Control_reg_addr), .eq(comparator_3_eq));  // open: gt, lt
  Register #(.width(16)) register_1 (.D(bus_data_in), .en(and_1_out), .Q(RAM_paragraph), .clk(Clock));  // open: clr
  Register #(.width(16)) _1st (.D(bus_data_in), .en(and_2_out), .Q(Sector_no[15:0]), .clk(Clock));  // open: clr
  Register #(.width(16)) _2nd (.D(bus_data_in), .en(and_3_out), .Q(Sector_no[31:16]), .clk(Clock));  // open: clr
  and and_4 (RAM_address_t, io, comparator_1_eq);
  and and_5 (_2_sector, io, comparator_4_eq);
  Comparator #(.width(12)) comparator_4 (.a(Address), .b(adder_1_out), .eq(comparator_4_eq));  // open: gt, lt
  and and_6 (_1_sector, io, comparator_2_eq);
  and and_7 (Control_register_t, io, comparator_3_eq);
  assign io_ack = io_ack_t ? 1'b1 : 1'bz;  // Controlled_Buffer controlled_buffer_2
  or or_1 (or_1_out, RAM_address_t, _2_sector);
  or or_2 (io_ack_t, or_1_out, or_3_out);
  or or_3 (or_3_out, _1_sector, Control_register_t);
  not not_5 (not_5_out, rd_wr_prime);
  Counter #(.trigger("falling")) counter_1 (
    .count(Control_register[0]), .Q(Counter), .carry(End), .clk(Clock_t));  // open: load, D, clr
  Priority_Encoder #(.select(2), .disabled(0)) priority_encoder_1 (
    .in0(RAM_address_t), .in1(_1_sector), .in2(_2_sector), .in3(Control_register_t),
    .out(priority_encoder_1_out), .gs(priority_encoder_1_gs));  // open: en_out, en_in
  Multiplexer #(.width(16)) multiplexer_1 (
    .in0(bus_data_in), .in1({Control_register[15:3], Device_rd_wr_prime, Control_register[1], 1'b0}),
    .out(multiplexer_1_out), .sel(End));  // open: en
  or or_4 (or_4_out, End, and_8_out);
  and and_8 (and_8_out, not_5_out, Control_register_t);
  Multiplexer #(.select(2), .width(16), .enable("false")) multiplexer_2 (
    .in0(RAM_paragraph), .in1(Sector_no[15:0]), .in2(Sector_no[31:16]),
    .in3({Control_register[15:3], Device_rd_wr_prime, Control_register[1:0]}), .out(multiplexer_2_out),
    .sel(priority_encoder_1_out));
  assign bit_extender_1_out = {{4{1'b0}}, RAM_paragraph};  // Bit_Extender bit_extender_1
  Register #(.width(16), .trigger("falling")) u_Control_register (
    .D(multiplexer_1_out), .en(or_4_out),
    .Q({Control_register[15:3], Device_rd_wr_prime, Control_register[1:0]}), .clk(Clock));  // open: clr
  not not_6 (not_6_out, mem);
  assign bit_extender_2_out = {{23{1'b0}}, {Counter, 1'b0}};  // Bit_Extender bit_extender_2
  Shifter #(.width(32)) shifter_1 (.in(Sector_no), .\dist (5'b01001), .out(shifter_1_out));
  Multiplexer #(.width(16)) multiplexer_3 (
    .in0(device_data_in), .in1(multiplexer_2_out), .out(bus_data_out), .sel(mem), .en(or_5_out));
  or or_5 (or_5_out, and_10_out, and_9_out);
  and and_9 (and_9_out, mem_2, Device_rd_wr_prime);
  and and_10 (and_10_out, rd_wr_prime, priority_encoder_1_gs);
  assign bit_extender_3_out = {{11{1'b0}}, {Counter, 1'b0}};  // Bit_Extender bit_extender_3
  Shifter #(.width(20)) shifter_2 (.in(bit_extender_1_out), .\dist (5'b00100), .out(shifter_2_out));
  not not_7 (not_7_out, Control_register[1]);
  and and_11 (mem_2, not_6_out, Control_register[0]);
  not not_8 (RAM_rd_wr_prime, Device_rd_wr_prime);
  Adder #(.width(32)) adder_2 (.a(bit_extender_2_out), .b(shifter_1_out), .out(Device_address));  // open: cin, cout
  not not_9 (not_9_out, Device_rd_wr_prime);
  assign device_data_out = not_9_out ? bus_data_in : 16'bz;  // Controlled_Buffer controlled_buffer_3
  Adder #(.width(20)) adder_3 (.a(bit_extender_3_out), .b(shifter_2_out), .out(RAM_address));  // open: cin, cout
  S_R_Flip_Flop s_r_ff_1 (.S(End), .clk(Clock_t), .R(iack), .Q(IRQ), .en(not_7_out));  // open: Qn, preset, reset

  // Other names for the same wires on the sheet: Bus_in[15:0] = bus_data_in; Clock_no_gate = Clock;
  //   Running = Control_register[0]; Inhibit_IRQ = Control_register[1]; Control_register[2] = Device_rd_wr_prime;
  //   Device_to_bus = Device_rd_wr_prime; Device_in[15:0] = device_data_in; mem_out = mem_2

  // Notes on the sheet:
  //   Constants
  //   RAM Address
  //   Sector number
endmodule

module int_arbiter (
  input  [5:0] vec_in,
  input  irq_in,
  input  ack_in,
  input  req,
  output [5:0] vec_out,
  output ack,
  output irq_out,
  output nop,
  output req_2,
  output ack_2,
  output ack_out
);

  wire and_1_out, and_2_out, and_3_out, and_4_out, not_1_out, not_2_out, not_3_out, or_1_out;
  wire [1:0] counter_1_q;

  Decoder #(.select(2), .enable("false")) decoder_1 (
    .out0(nop), .out1(req_2), .out2(ack), .sel(counter_1_q));  // open: out3
  Counter #(.width(2), .max('h2)) counter_1 (.Q(counter_1_q), .clk(or_1_out));  // open: load, D, count, carry, clr
  or or_1 (or_1_out, and_1_out, and_2_out, and_3_out);
  assign vec_out = ack ? vec_in : 6'bz;  // Controlled_Buffer controlled_buffer_1
  and and_1 (and_1_out, ack, not_1_out);
  not not_1 (not_1_out, ack_in);
  or or_2 (irq_out, and_4_out, not_2_out);
  and and_2 (and_2_out, req_2, ack_in);
  not not_2 (not_2_out, nop);
  and and_3 (and_3_out, nop, req, not_3_out);
  and and_4 (and_4_out, irq_in, nop);
  not not_3 (not_3_out, ack_in);
  and and_5 (ack_out, nop, ack_in);

  assign ack_2 = ack;

  // Notes on the sheet:
  //   req: pull=down
  //   irq_in: pull=down
  //   ack_in: pull=down
endmodule

module timer (
  input  [15:0] data_in,
  input  [11:0] address,
  input  [11:0] io_address,
  input  io_sel,
  input  rd_wr_prime,
  input  clk,
  input  iack,
  output [15:0] data_out,
  output [15:0] mon,
  output irq,
  output io_ack
);

  wire and_4_out, comparator_1_eq, io_ack_t, not_1_out, or_1_out, overflow, read, s_r_ff_1_q, write;

  assign io_ack = io_ack_t ? 1'b1 : 1'bz;  // Controlled_Buffer controlled_buffer_1
  Comparator #(.width(12)) comparator_1 (.a(address), .b(io_address), .eq(comparator_1_eq));  // open: gt, lt
  and and_1 (io_ack_t, comparator_1_eq, io_sel);
  and and_2 (write, ~rd_wr_prime, io_ack_t);  // AND_Gate
  and and_3 (read, io_ack_t, rd_wr_prime);
  not not_1 (not_1_out, write);
  S_R_Flip_Flop #(.trigger("falling")) s_r_ff_1 (
    .S(write), .clk(clk), .R(overflow), .Q(s_r_ff_1_q));  // open: Qn, preset, reset, en
  assign data_out = read ? mon : 16'bz;  // Controlled_Buffer controlled_buffer_2
  Counter #(.width(16), .max('hffff), .ongoal("stay"), .trigger("falling")) counter_1 (
    .load(1'b1), .D(data_in), .count(not_1_out), .Q(mon), .carry(overflow), .clk(clk));  // open: clr
  and and_4 (and_4_out, s_r_ff_1_q, overflow);
  or or_1 (or_1_out, iack, write);
  S_R_Flip_Flop #(.trigger("falling")) s_r_ff_2 (
    .S(and_4_out), .clk(clk), .R(or_1_out), .Q(irq));  // open: Qn, preset, reset, en

  // Notes on the sheet:
  //   rd_wr_prime: pull=down
  //   io_sel: pull=down
  //   iack: pull=down
  //   clk: pull=down
endmodule

module register (
  input  [15:0] data_in,
  input  [11:0] address,
  input  [11:0] io_address,
  input  io_sel,
  input  rd_wr_prime,
  input  clk,
  output [15:0] data_out,
  output [15:0] mon,
  output io_ack
);

  wire comparator_1_eq, io_ack_t, read, write;

  assign io_ack = io_ack_t ? 1'b1 : 1'bz;  // Controlled_Buffer controlled_buffer_1
  Comparator #(.width(12)) comparator_1 (.a(address), .b(io_address), .eq(comparator_1_eq));  // open: gt, lt
  and and_1 (io_ack_t, comparator_1_eq, io_sel);
  and and_2 (write, ~rd_wr_prime, io_ack_t);  // AND_Gate
  and and_3 (read, io_ack_t, rd_wr_prime);
  Register #(.width(16), .trigger("falling")) register_1 (.D(data_in), .en(write), .Q(mon), .clk(clk));  // open: clr
  assign data_out = read ? mon : 16'bz;  // Controlled_Buffer controlled_buffer_2

  // Notes on the sheet:
  //   io_sel: pull=down
  //   clk: pull=down
  //   rd_wr_prime: pull=down
endmodule

module uart_controller (
  input  uart_dt,
  input  [7:0] uart_rx,
  input  uart_con,
  input  [15:0] data_in,
  input  [11:0] io_address,
  input  [11:0] base_address,
  input  word,
  input  io_sel,
  input  rd_wr_prime,
  input  clk,
  output uart_clk,
  output uart_rd_wr_prime,
  output uart_en,
  output [7:0] uart_tx,
  output [15:0] data_out,
  output irq,
  output io_ack
);

  wire comparator_1_eq, comparator_2_eq, d_ff_2_q, dr_read, dr_write, int_en, or_1_out, \сr_read ,
       \сr_select , \сr_write ;
  wire [7:0] multiplexer_1_out;
  wire [11:0] adder_1_out;

  assign io_ack = or_1_out ? 1'b1 : 1'bz;  // Controlled_Buffer controlled_buffer_1
  or or_1 (or_1_out, uart_en, \сr_select );
  Adder #(.width(12)) adder_1 (.a(base_address), .b(12'h1), .out(adder_1_out));  // open: cin, cout
  Comparator #(.width(12)) comparator_1 (.a(io_address), .b(base_address), .eq(comparator_1_eq));  // open: gt, lt
  Comparator #(.width(12)) comparator_2 (.a(io_address), .b(adder_1_out), .eq(comparator_2_eq));  // open: gt, lt
  and and_1 (uart_en, io_sel, comparator_1_eq);
  and and_2 (\сr_select , comparator_2_eq, io_sel);
  and and_3 (dr_write, ~rd_wr_prime, uart_en);  // AND_Gate
  and and_4 (dr_read, uart_en, rd_wr_prime);
  and and_5 (\сr_write , ~rd_wr_prime, \сr_select );  // AND_Gate
  and and_6 (\сr_read , \сr_select , rd_wr_prime);
  Multiplexer #(.width(8), .enable("false")) multiplexer_1 (
    .in0({8{1'b0}}), .in1({uart_dt, uart_con, int_en, {5{1'b0}}}), .out(multiplexer_1_out), .sel(word));
  assign data_out = \сr_read  ? {{8{1'b0}}, uart_dt, uart_con, int_en, {5{1'b0}}} : 16'bz;  // Controlled_Buffer controlled_buffer_2
  Bit_Extender #(.in_width(16), .out_width(8)) bit_extender_1 (.in(data_in), .out(uart_tx));
  D_Flip_Flop #(.trigger("falling")) d_ff_1 (
    .clk(clk), .D(data_in[5]), .Q(int_en), .en(\сr_write ));  // open: Qn, preset, reset
  assign data_out = dr_read ? {multiplexer_1_out, uart_rx} : 16'bz;  // Controlled_Buffer controlled_buffer_3
  D_Flip_Flop #(.trigger("falling")) d_ff_2 (.clk(clk), .D(uart_dt), .Q(d_ff_2_q));  // open: Qn, preset, en, reset
  and and_7 (irq, uart_dt, int_en, ~d_ff_2_q);  // AND_Gate

  assign uart_clk = clk;
  assign uart_rd_wr_prime = rd_wr_prime;

  // Other names for the same wires on the sheet: dr_select = uart_en; io_select = io_sel; io_word = word

  // Notes on the sheet:
  //   rd_wr_prime: pull=down
  //   clk: pull=down
  //   io_sel: pull=down
  //   word: pull=down
endmodule

module single_step (
  input  btn_stop,
  input  btn_run,
  input  btn_step,
  input  clk,
  input  fetch,
  output stop,
  output hold,
  output run
);

  wire and_1_out, and_2_out, and_3_out, not_1_out, not_2_out, or_1_out;

  not not_1 (not_1_out, btn_step);
  D_Flip_Flop d_ff_1 (.Q(stop), .Qn(run), .preset(btn_stop), .reset(btn_run));  // open: clk, D, en
  and and_1 (and_1_out, btn_step, not_1_out);
  not not_2 (not_2_out, fetch);
  or or_1 (or_1_out, btn_run, and_1_out);
  and and_2 (and_2_out, stop, and_3_out);
  and and_3 (and_3_out, fetch, not_2_out);
  S_R_Flip_Flop s_r_ff_1 (.Q(hold), .preset(and_2_out), .reset(or_1_out));  // open: S, clk, R, Qn, en
endmodule
